// Logisim project 16-bit-datapath.circ as structural Verilog: 4 circuits, main circuit Datapath
module Datapath (
  input  in_1,
  output [3:0] Opcode,
  output [3:0] RD,
  output [3:0] RS,
  output [3:0] RT_Im,
  output out_6,
  output [15:0] Result
);

  wire alu_1_zero, and_1_out, clock_1_out, control_unit_1_b_inv, control_unit_1_branch, control_unit_1_c_in,
       control_unit_1_jump, control_unit_1_load, control_unit_1_ram_to_reg, control_unit_1_reg_writeen,
       control_unit_1_rt_im, control_unit_1_store;
  wire [1:0] control_unit_1_alu_op;
  wire [15:0] adder_1_out, adder_2_out, alu_1_result, bit_extender_1_out, bit_extender_2_out,
       multiplexer_1_out, multiplexer_2_out, multiplexer_3_out, multiplexer_4_out, ram_1_data, register_1_q,
       register_2_rd_data, register_2_rs_data, register_2_rt_data;

  Clock clock_1 (.out(clock_1_out));
  Register_part #(.width(16)) register_1 (.D(multiplexer_4_out), .Q(register_1_q), .clk(clock_1_out));  // open: en, clr
  Control_Unit control_unit_1 (
    .Opcode(Opcode), .Reg_WriteEn(control_unit_1_reg_writeen), .C_in(control_unit_1_c_in),
    .ALU_op(control_unit_1_alu_op), .B_inv(control_unit_1_b_inv), .RT_Im(control_unit_1_rt_im),
    .RAM_To_Reg(control_unit_1_ram_to_reg), .Branch(control_unit_1_branch), .Load(control_unit_1_load),
    .Store(control_unit_1_store), .Jump(control_unit_1_jump));
  Adder #(.width(16)) adder_1 (.a(16'h1), .b(register_1_q), .out(adder_1_out), .cin(1'b0));  // open: cout
  ROM #(.addrWidth(16), .dataWidth(16)) rom_1 (.addr(register_1_q), .data({Opcode, RD, RS, RT_Im}));  // open: sel
  assign bit_extender_1_out = {{4{1'b0}}, {RD, RS, RT_Im}};  // Bit_Extender bit_extender_1
  Register register_2 (
    .Write_Data(Result), .Write_Location(RD), .RS_Data(register_2_rs_data), .RT_Data(register_2_rt_data),
    .RS(RS), .Clock(clock_1_out), .RT(RT_Im), .Write_En(control_unit_1_reg_writeen),
    .RD_Data(register_2_rd_data));
  Multiplexer #(.width(16), .enable("false")) multiplexer_1 (
    .in0(register_2_rt_data), .in1(bit_extender_2_out), .out(multiplexer_1_out), .sel(control_unit_1_rt_im));
  assign bit_extender_2_out = {{12{1'b0}}, RT_Im};  // Bit_Extender bit_extender_2
  Multiplexer #(.width(16), .enable("false")) multiplexer_2 (
    .in0(multiplexer_1_out), .in1(register_2_rd_data), .out(multiplexer_2_out), .sel(control_unit_1_branch));
  ALU alu_1 (
    .A(register_2_rs_data), .B(multiplexer_2_out), .B_inv(control_unit_1_b_inv), .C_in(control_unit_1_c_in),
    .C_out(out_6), .ALU_op(control_unit_1_alu_op), .Result(alu_1_result), .Zero(alu_1_zero));
  Adder #(.width(16)) adder_2 (.a(adder_1_out), .b(bit_extender_2_out), .out(adder_2_out));  // open: cin, cout
  and and_1 (and_1_out, alu_1_zero, control_unit_1_branch);
  Multiplexer #(.width(16), .enable("false")) multiplexer_3 (
    .in0(adder_1_out), .in1(adder_2_out), .out(multiplexer_3_out), .sel(and_1_out));
  Multiplexer #(.width(16), .enable("false")) multiplexer_4 (
    .in0(multiplexer_3_out), .in1(bit_extender_1_out), .out(multiplexer_4_out), .sel(control_unit_1_jump));
  Multiplexer #(.width(16), .enable("false")) multiplexer_5 (
    .in0(alu_1_result), .in1(ram_1_data), .out(Result), .sel(control_unit_1_ram_to_reg));
  RAM #(.addrWidth(16), .dataWidth(16), .bus("separate")) ram_1 (
    .addr(alu_1_result), .din(register_2_rd_data), .data(ram_1_data), .str(control_unit_1_store),
    .clk(clock_1_out), .ld(control_unit_1_load), .clr(in_1));  // open: sel

  // Notes on the sheet:
  //   ROM (Inst. Memory)
  //   RAM (Data Memory)
endmodule

module Register (
  input  [15:0] Write_Data,
  input  Write_En,
  input  [3:0] Write_Location,
  input  Clock,
  input  [3:0] RS,
  input  [3:0] RT,
  output [15:0] RS_Data,
  output [15:0] RT_Data,
  output [15:0] RD_Data
);

  wire decoder_1_out0, decoder_1_out1, decoder_1_out2, decoder_1_out3, decoder_1_out4, decoder_1_out5,
       decoder_1_out6, decoder_1_out7, decoder_1_out8, decoder_1_out9, decoder_1_out10, decoder_1_out11,
       decoder_1_out12, decoder_1_out13, decoder_1_out14, decoder_1_out15;
  wire [15:0] r0_q, r1_q, r2_q, r3_q, r4_q, r5_q, r6_q, r7_q, r8_q, r9_q, r10_q, r11_q, r12_q, r13_q, r14_q,
       r15_q;

  Decoder #(.select(4), .disabled(0)) decoder_1 (
    .out0(decoder_1_out0), .out1(decoder_1_out1), .out2(decoder_1_out2), .out3(decoder_1_out3),
    .out4(decoder_1_out4), .out5(decoder_1_out5), .out6(decoder_1_out6), .out7(decoder_1_out7),
    .out8(decoder_1_out8), .out9(decoder_1_out9), .out10(decoder_1_out10), .out11(decoder_1_out11),
    .out12(decoder_1_out12), .out13(decoder_1_out13), .out14(decoder_1_out14), .out15(decoder_1_out15),
    .sel(Write_Location), .en(Write_En));
  Register_part #(.width(16)) r0 (.D(Write_Data), .en(decoder_1_out0), .Q(r0_q), .clk(Clock));  // open: clr
  Register_part #(.width(16)) r1 (.D(Write_Data), .en(decoder_1_out1), .Q(r1_q), .clk(Clock));  // open: clr
  Register_part #(.width(16)) r2 (.D(Write_Data), .en(decoder_1_out2), .Q(r2_q), .clk(Clock));  // open: clr
  Register_part #(.width(16)) r3 (.D(Write_Data), .en(decoder_1_out3), .Q(r3_q), .clk(Clock));  // open: clr
  Register_part #(.width(16)) r4 (.D(Write_Data), .en(decoder_1_out4), .Q(r4_q), .clk(Clock));  // open: clr
  Register_part #(.width(16)) r5 (.D(Write_Data), .en(decoder_1_out5), .Q(r5_q), .clk(Clock));  // open: clr
  Register_part #(.width(16)) r6 (.D(Write_Data), .en(decoder_1_out6), .Q(r6_q), .clk(Clock));  // open: clr
  Register_part #(.width(16)) r7 (.D(Write_Data), .en(decoder_1_out7), .Q(r7_q), .clk(Clock));  // open: clr
  Register_part #(.width(16)) r8 (.D(Write_Data), .en(decoder_1_out8), .Q(r8_q), .clk(Clock));  // open: clr
  Register_part #(.width(16)) r9 (.D(Write_Data), .en(decoder_1_out9), .Q(r9_q), .clk(Clock));  // open: clr
  Register_part #(.width(16)) r10 (.D(Write_Data), .en(decoder_1_out10), .Q(r10_q), .clk(Clock));  // open: clr
  Register_part #(.width(16)) r11 (.D(Write_Data), .en(decoder_1_out11), .Q(r11_q), .clk(Clock));  // open: clr
  Register_part #(.width(16)) r12 (.D(Write_Data), .en(decoder_1_out12), .Q(r12_q), .clk(Clock));  // open: clr
  Register_part #(.width(16)) r13 (.D(Write_Data), .en(decoder_1_out13), .Q(r13_q), .clk(Clock));  // open: clr
  Register_part #(.width(16)) r14 (.D(Write_Data), .en(decoder_1_out14), .Q(r14_q), .clk(Clock));  // open: clr
  Register_part #(.width(16)) r15 (.D(Write_Data), .en(decoder_1_out15), .Q(r15_q), .clk(Clock));  // open: clr
  Multiplexer #(.select(4), .width(16), .enable("false")) multiplexer_1 (
    .in0(r0_q), .in1(r1_q), .in2(r2_q), .in3(r3_q), .in4(r4_q), .in5(r5_q), .in6(r6_q), .in7(r7_q),
    .in8(r8_q), .in9(r9_q), .in10(r10_q), .in11(r11_q), .in12(r12_q), .in13(r13_q), .in14(r14_q),
    .in15(r15_q), .out(RS_Data), .sel(RS));
  Multiplexer #(.select(4), .width(16), .enable("false")) multiplexer_2 (
    .in0(r0_q), .in1(r1_q), .in2(r2_q), .in3(r3_q), .in4(r4_q), .in5(r5_q), .in6(r6_q), .in7(r7_q),
    .in8(r8_q), .in9(r9_q), .in10(r10_q), .in11(r11_q), .in12(r12_q), .in13(r13_q), .in14(r14_q),
    .in15(r15_q), .out(RT_Data), .sel(RT));
  Multiplexer #(.select(4), .width(16), .enable("false")) multiplexer_3 (
    .in0(r0_q), .in1(r1_q), .in2(r2_q), .in3(r3_q), .in4(r4_q), .in5(r5_q), .in6(r6_q), .in7(r7_q),
    .in8(r8_q), .in9(r9_q), .in10(r10_q), .in11(r11_q), .in12(r12_q), .in13(r13_q), .in14(r14_q),
    .in15(r15_q), .out(RD_Data), .sel(Write_Location));
endmodule

module Control_Unit (
  input  [3:0] Opcode,
  output Reg_WriteEn,
  output RT_Im,
  output B_inv,
  output C_in,
  output [1:0] ALU_op,
  output RAM_To_Reg,
  output Branch,
  output Jump,
  output Load,
  output Store
);

  wire add0001_out, addi0010_out, and0100_out, sll0111_out, slt1000_out, sub0000_out;

  and sub0000 (sub0000_out, ~Opcode[3], ~Opcode[2], ~Opcode[1], ~Opcode[0]);  // AND_Gate
  and add0001 (add0001_out, ~Opcode[3], ~Opcode[2], ~Opcode[1], Opcode[0]);  // AND_Gate
  and addi0010 (addi0010_out, ~Opcode[3], ~Opcode[2], Opcode[1], ~Opcode[0]);  // AND_Gate
  and jmp0011 (Jump, ~Opcode[3], ~Opcode[2], Opcode[1], Opcode[0]);  // AND_Gate
  and and0100 (and0100_out, ~Opcode[3], Opcode[2], ~Opcode[1], ~Opcode[0]);  // AND_Gate
  and beq0110 (Branch, ~Opcode[3], Opcode[2], Opcode[1], ~Opcode[0]);  // AND_Gate
  and lw0101 (Load, ~Opcode[3], Opcode[2], ~Opcode[1], Opcode[0]);  // AND_Gate
  and sll0111 (sll0111_out, ~Opcode[3], Opcode[2], Opcode[1], Opcode[0]);  // AND_Gate
  and slt1000 (slt1000_out, Opcode[3], ~Opcode[2], ~Opcode[1], ~Opcode[0]);  // AND_Gate
  and sw1001 (Store, Opcode[3], ~Opcode[2], ~Opcode[1], Opcode[0]);  // AND_Gate
  or or_1 (ALU_op[0], and0100_out, slt1000_out);
  or or_2 (ALU_op[1], sll0111_out, slt1000_out);
  or or_3 (Reg_WriteEn, sub0000_out, add0001_out, addi0010_out, and0100_out, Load, sll0111_out, slt1000_out);
  or or_4 (RT_Im, addi0010_out, Load, Store);
  or or_5 (B_inv, sub0000_out, Branch);
  or or_6 (C_in, sub0000_out, Branch);

  assign RAM_To_Reg = Load;
endmodule

module ALU (
  input  C_in,
  input  [15:0] A,
  input  [15:0] B,
  input  B_inv,
  input  [1:0] ALU_op,
  output C_out,
  output [15:0] Result,
  output Zero
);

  wire comparator_1_lt, or_1_out;
  wire [3:0] bit_extender_1_out;
  wire [15:0] adder_1_out, and_1_out, bit_extender_2_out, multiplexer_1_out, not_1_out, shifter_1_out;

  Multiplexer #(.width(16), .enable("false")) multiplexer_1 (
    .in0(B), .in1(not_1_out), .out(multiplexer_1_out), .sel(B_inv));
  assign not_1_out = ~B;  // NOT_Gate not_1, 16 bits wide
  Bit_Extender #(.in_width(16), .out_width(4)) bit_extender_1 (.in(multiplexer_1_out), .out(bit_extender_1_out));
  Adder #(.width(16)) adder_1 (.a(A), .b(multiplexer_1_out), .out(adder_1_out), .cin(C_in), .cout(C_out));
  assign and_1_out = A & multiplexer_1_out;  // AND_Gate and_1, 16 bits wide
  Shifter #(.width(16)) shifter_1 (.in(A), .\dist (bit_extender_1_out), .out(shifter_1_out));
  Comparator #(.width(16)) comparator_1 (.a(A), .b(multiplexer_1_out), .lt(comparator_1_lt));  // open: gt, eq
  assign bit_extender_2_out = {{15{1'b0}}, comparator_1_lt};  // Bit_Extender bit_extender_2
  Multiplexer #(.select(2), .width(16), .enable("false")) multiplexer_2 (
    .in0(adder_1_out), .in1(and_1_out), .in2(shifter_1_out), .in3(bit_extender_2_out), .out(Result),
    .sel(ALU_op));
  or or_1 (or_1_out, Result[0], Result[1], Result[2], Result[3], Result[4], Result[5], Result[6], Result[7], Result[8], Result[9], Result[10], Result[11], Result[12], Result[13], Result[14], Result[15]);
  not not_2 (Zero, or_1_out);
endmodule
